# Fritzing sketch 00 (saved by Fritzing 0.9.3b)
circuit board: 8.46667cm x 5.64444cm
breadboards: 1

parts:
  LED2 = LED - 3mm [color="Red (635nm)" package="3 mm [THT]"]
  LED_IR = LED - 3mm [color="Infrared (940nm)" package="3 mm [THT]"]
  U1 = ESP8266 WiFi Module [part_number=ESP8266]
  Componente1 = 4N25 [package=THT]

nets:
  N1: LED2.cathode, LED_IR.cathode, U1.GND, Componente1.Pin_1
  N2: LED2.anode, U1.GPIO_0
  N3: LED_IR.anode, Componente1.Pin_4
  N4: U1.GPIO_2, Componente1.Pin_2

custom parts:
  ESP8266 WiFi Module: Generic WiFi Module based on the ESP8266 with onboard PCB antenna and UART communications
  4N25: Optocoupler
